// Digital circuit hw3_c.dig as structural Verilog
module hw3_c (
  input  [3:0] X,
  input  [3:0] Y,
  input  _0,
  input  [3:0] _4,
  input  [3:0] _6,
  output [3:0] Z
);

  wire comparator_1_lt;
  wire [3:0] add_1_s, add_2_s;

  Add #(.Bits(4)) add_1 (.a(X), .b(_4), .c_i(_0), .s(add_1_s));  // open: c_o
  Add #(.Bits(4)) add_2 (.a(Y), .b(_6), .c_i(_0), .s(add_2_s));  // open: c_o
  Comparator #(.Bits(4)) comparator_1 (.a(X), .b(Y), .lt(comparator_1_lt));  // open: gt, eq
  Multiplexer #(.Bits(4)) multiplexer_1 (.sel(comparator_1_lt), .in_0(add_2_s), .in_1(add_1_s), .out(Z));
endmodule
