// Digital circuit hw3_d.dig as structural Verilog
module hw3_d (
  input  [3:0] X,
  input  [3:0] _5,
  input  _0,
  input  [3:0] Y,
  input  [3:0] _6,
  output [3:0] Z
);

  wire comparator_1_gt;
  wire [3:0] add_1_s, add_2_s;

  Add #(.Bits(4)) add_1 (.a(X), .b(_5), .c_i(_0), .s(add_1_s));  // open: c_o
  Add #(.Bits(4)) add_2 (.a(Y), .b(_6), .c_i(_0), .s(add_2_s));  // open: c_o
  Comparator #(.Bits(4)) comparator_1 (.a(X), .b(Y), .gt(comparator_1_gt));  // open: eq, lt
  Multiplexer #(.Bits(4)) multiplexer_1 (.sel(comparator_1_gt), .in_0(add_2_s), .in_1(add_1_s), .out(Z));
endmodule
